# Fritzing sketch esp_temp (saved by Fritzing 0.9.3b)
breadboards: 1

parts:
  U1 = ESP8266 WiFi Module [part_number=ESP8266]
  DS1 = DS18B20 1-Wire Temperature Sensor [part_number=DS18B20]
  R1 = Resistor [tolerance=±5% resistance=220 package="0603 [SMD]"]
  Part1 = Arduino Uno (Rev3)

nets:
  N1: U1.RXD, Part1.D1/TX
  VCC: U1.VCC, U1.CH_PD, U1.REST, DS1.VDD, R1.Pin_0, Part1.3V3
  N2: U1.GPIO_2, DS1.DQ, R1.Pin_1
  GND: U1.GND, DS1.GND, Part1.GND
  N3: U1.TXD, Part1.D0/RX
